# Fritzing sketch ESP-12E-Running (saved by Fritzing 0.9.3b)
circuit board: 6.07072cm x 5.46847cm
breadboards: 1

parts:
  ESP12E = Gizwits WiFi Witty ESP-12F
  JACK1 = 2.1mm Barrel Jack with Terminal Block
  R3 = Resistor [tolerance=±5% resistance=10k package="1206 [SMD]"]
  R4 = Resistor [tolerance=±5% resistance=10k package="1206 [SMD]"]
  C1 = Capacitor [package=cap-pth-small-kit]
  R5 = Resistor [tolerance=±5% resistance=10k package="1206 [SMD]"]
  R6 = Resistor [tolerance=±5% resistance=10k package="1206 [SMD]"]

nets:
  3.3V: ESP12E.REST, ESP12E.VCC, JACK1.POS, R3.Pin_0, C1.1, R5.Pin_0, R5.Pin_1, R6.Pin_1
  N1: ESP12E.CH_PD, R6.Pin_0
  GND: ESP12E.GND, JACK1.NEG, R4.Pin_0, C1.2
  N2: ESP12E.GPIO0, R3.Pin_1
  N3: ESP12E.GPIO5, R4.Pin_1
