# Fritzing sketch SimpleLED-PCB (saved by Fritzing 0.9.3b)
circuit board: 3.24662cm x 1.27856cm
breadboards: 1

parts:
  LED1 = smd LED [color="Red (633nm)" package="0603 [SMD]"]
  R1 = Resistor [tolerance=±5% resistance=220 package="0402 [SMD]"]
  JACK1 = 2.1mm Barrel Jack with Terminal Block

nets:
  N1: LED1.cathode, R1.Pin_1
  N2: LED1.anode, JACK1.POS
  N3: R1.Pin_0, JACK1.NEG

notes:
  LED
