# Fritzing sketch WaterSystem (saved by Fritzing 0.9.3b)
circuit board: 8.63587cm x 5.015cm
breadboards: 1

parts:
  JACK1 = 2.1mm Barrel Jack with Terminal Block
  R1 = Resistor [tolerance=±5% resistance=10k package="2010 [SMD]"]
  R2 = Resistor [tolerance=±5% resistance=10k package="2010 [SMD]"]
  R4 = Resistor [tolerance=±5% resistance=10k package="2010 [SMD]"]
  R5 = Resistor [tolerance=±5% resistance=10k package="2010 [SMD]"]
  C1 = Ceramic Capacitor [capacitance="100 nF" package="1206 [SMD, multilayer]"]
  J1 = Camdenboss CTB0158-4 [part_number=CTB0158-4 package=THT]
  Q1 = NPN-Transistor [package="TO92 [THT]"]
  R6 = Resistor [tolerance=±5% resistance=10k package="2010 [SMD]"]
  JACK2 = 2.1mm Barrel Jack with Terminal Block
  J2 = Camdenboss CTB0158-2 [part_number=CTB0158-2 package=THT]
  D1 = Rectifier Diode [part_number=1N4001 package="300 mil [THT]"]
  U1 = ESP8266 WiFi Module [part_number=ESP8266]

nets:
  N1: JACK1.POS, R1.Pin_0, R2.Pin_0, R4.Pin_1, C1.0, J1.pin4, U1.VCC
  N2: JACK1.NEG, R5.Pin_1, C1.1, J1.pin3, Q1.E, JACK2.NEG, U1.GND
  N3: R1.Pin_1, U1.REST
  N4: R2.Pin_1, U1.CH_PD
  N5: R4.Pin_0, U1.GPIO_0
  N6: R5.Pin_0, U1.GPIO_15
  N7: J1.pin1, U1.ADC_0
  N8: Q1.B, R6.Pin_1
  N9: Q1.C, J2.pin2, D1.anode
  N10: R6.Pin_0, U1.GPIO_4
  N11: JACK2.POS, J2.pin1, D1.cathode
