# Fritzing sketch arduino-relay-trans (saved by Fritzing 0.9.3b)
breadboards: 1

parts:
  Part1 = Arduino Uno (Rev3)
  10k_ohms = Resistor [tolerance=±5% resistance=220 package="2010 [SMD]"]
  100k_Ohms = Resistor [tolerance=±5% resistance=220 package="2010 [SMD]"]
  Q1 = TRANSISTOR_NPN [package=to-92-ammo]
  10k_Ohms = Resistor [tolerance=±5% resistance=220 package="2010 [SMD]"]

nets:
  N1: Part1.D7, 10k_ohms.Pin_0, 100k_Ohms.Pin_1
  N2: Part1.5V, 10k_Ohms.Pin_1
  N3: 10k_ohms.Pin_1, Q1.B
  GND: 100k_Ohms.Pin_0, Q1.E
  net label: Q1.C, 10k_Ohms.Pin_0
