# Fritzing sketch atmega16-powerup-16mhz (saved by Fritzing 0.9.3b)

parts:
  MCU = ATmega16 [package="DIP (Dual Inline)"]
  C1 = Ceramic Capacitor [capacitance=100nF package="100 mil [THT, multilayer]"]  # not connected
  C2_22pF = Ceramic Capacitor [capacitance=100nF package="100 mil [THT, multilayer]"]
  C3_22pF = Ceramic Capacitor [capacitance=100nF package="100 mil [THT, multilayer]"]
  XTAL1 = Crystal [frequency="16 Mhz" package=THT]

nets:
  5V: MCU.PIN_10
  GND: MCU.PIN_11, C3_22pF.0
  N1: MCU.PIN_12, C2_22pF.1, XTAL1.pin_0
  N2: MCU.PIN_13, C3_22pF.1, XTAL1.pin_1

notes:
  ATmega16 power up circuit

custom parts:
  ATmega16: ATmega16 - 40 pins, 600 mil dual inline package (DIP)
