# Fritzing sketch attiny85_powerup-ext-clock (saved by Fritzing 0.9.3b)
circuit board: 8.46667cm x 5.64444cm

parts:
  U1 = attiny85 [package=dip]
  C1 = Ceramic Capacitor [capacitance=100nF package="100 mil [THT, multilayer]"]

nets:
  net label: U1.Pin_3
  GND: U1.Pin_4, C1.0
  5V: U1.Pin_8, C1.1

notes:
  attiny85 port 3 connects to LTC1799 Port 5
